// Logisim project Assignment 1.circ as structural Verilog: 1 circuit, main circuit main
module main (
  input  in_1
);

  wire and_1_out, and_2_out, and_3_out, and_4_out, and_5_out, and_6_out, and_7_out, and_8_out, and_9_out,
       and_10_out, and_11_out, and_12_out, and_13_out, and_14_out, and_15_out, and_16_out, and_17_out,
       and_18_out, and_19_out, and_20_out, and_21_out, and_22_out, and_23_out, and_24_out, and_25_out,
       and_26_out, and_27_out, and_28_out, and_29_out, and_30_out, and_31_out, and_32_out, and_33_out,
       and_34_out, and_35_out, and_36_out, and_37_out, and_38_out, and_39_out, and_40_out, and_41_out,
       and_42_out, and_43_out, and_44_out, and_45_out, buffer_1_out, buffer_2_out, button_1_out,
       button_2_out, button_3_out, button_4_out, button_5_out, button_6_out, d_ff_1_q, d_ff_2_q, d_ff_3_q,
       d_ff_4_q, d_ff_5_q, d_ff_6_q, d_ff_7_q, d_ff_8_q, j_k_ff_1_q, j_k_ff_1_qn, j_k_ff_2_qn, j_k_ff_3_qn,
       j_k_ff_4_qn, j_k_ff_5_qn, j_k_ff_6_qn, j_k_ff_7_qn, nand_1_out, nand_2_out, nand_3_out, nand_4_out,
       nand_5_out, nand_6_out, nand_7_out, nor_1_out, nor_2_out, nor_3_out, not_1_out, not_2_out, not_3_out,
       not_4_out, not_5_out, not_6_out, not_7_out, not_8_out, not_9_out, not_10_out, not_11_out, not_12_out,
       not_13_out, not_14_out, not_15_out, not_16_out, not_17_out, not_18_out, not_19_out, not_20_out,
       not_21_out, or_1_out, or_2_out, or_3_out, or_4_out, or_5_out, or_6_out, or_7_out, or_8_out, or_9_out,
       or_10_out, or_11_out, or_12_out, or_13_out, or_14_out, or_15_out, or_16_out, or_17_out, or_18_out,
       or_19_out, or_20_out, or_21_out, or_22_out, or_23_out, or_24_out, or_25_out;
  wire [3:0] and_46_out, and_47_out, j_k_ff_2_q, j_k_ff_3_q;

  Button button_1 (.out(button_1_out));
  Button button_2 (.out(button_2_out));
  Button button_3 (.out(button_3_out));
  Button button_4 (.out(button_4_out));
  or or_1 (or_1_out, button_2_out, button_1_out);
  Button button_5 (.out(button_5_out));
  Button button_6 (.out(button_6_out));
  and and_1 (and_1_out, or_1_out, in_1);
  or or_2 (or_2_out, button_1_out, d_ff_1_q);
  or or_3 (or_3_out, button_1_out, d_ff_2_q);
  or or_4 (or_4_out, button_1_out, d_ff_3_q);
  or or_5 (or_5_out, button_1_out, d_ff_4_q);
  or or_6 (or_6_out, button_1_out, d_ff_5_q);
  or or_7 (or_7_out, button_1_out, d_ff_6_q);
  or or_8 (or_8_out, button_1_out, d_ff_7_q);
  or or_9 (or_9_out, button_1_out, d_ff_8_q);
  or or_10 (or_10_out, button_3_out, button_4_out);
  J_K_Flip_Flop j_k_ff_1 (
    .J(or_10_out), .K(button_4_out), .clk(or_10_out), .Q(j_k_ff_1_q), .Qn(j_k_ff_1_qn), .reset(not_1_out));  // open: preset
  buf buffer_1 (buffer_1_out, and_1_out);
  and and_2 (and_2_out, d_ff_1_q, or_3_out);
  and and_3 (and_3_out, d_ff_2_q, or_4_out);
  and and_4 (and_4_out, d_ff_3_q, or_5_out);
  and and_5 (and_5_out, d_ff_4_q, or_6_out);
  and and_6 (and_6_out, d_ff_5_q, or_7_out);
  and and_7 (and_7_out, d_ff_6_q, or_8_out);
  and and_8 (and_8_out, d_ff_7_q, or_9_out);
  nor nor_1 (nor_1_out, button_5_out, nor_2_out);
  nor nor_2 (nor_2_out, nor_1_out, button_6_out);
  or or_11 (or_11_out, button_5_out, button_6_out);
  not not_1 (not_1_out, in_1);
  and and_9 (and_9_out, not_2_out, not_3_out, not_4_out, not_5_out, not_6_out, not_7_out, not_8_out, not_9_out, not_10_out);
  D_Flip_Flop d_ff_1 (.D(and_13_out), .clk(buffer_1_out), .Q(d_ff_1_q));  // open: Qn, preset, reset
  D_Flip_Flop d_ff_2 (.D(and_14_out), .clk(buffer_1_out), .Q(d_ff_2_q));  // open: Qn, preset, reset
  D_Flip_Flop d_ff_3 (.D(and_15_out), .clk(buffer_1_out), .Q(d_ff_3_q));  // open: Qn, preset, reset
  D_Flip_Flop d_ff_4 (.D(and_16_out), .clk(buffer_1_out), .Q(d_ff_4_q));  // open: Qn, preset, reset
  D_Flip_Flop d_ff_5 (.D(and_17_out), .clk(buffer_1_out), .Q(d_ff_5_q));  // open: Qn, preset, reset
  D_Flip_Flop d_ff_6 (.D(and_18_out), .clk(buffer_1_out), .Q(d_ff_6_q));  // open: Qn, preset, reset
  D_Flip_Flop d_ff_7 (.D(and_19_out), .clk(buffer_1_out), .Q(d_ff_7_q));  // open: Qn, preset, reset
  D_Flip_Flop d_ff_8 (.D(and_20_out), .clk(buffer_1_out), .Q(d_ff_8_q));  // open: Qn, preset, reset
  buf buffer_2 (buffer_2_out, or_11_out);
  not not_2 (not_2_out, j_k_ff_2_q[0]);
  not not_3 (not_3_out, j_k_ff_2_q[1]);
  not not_4 (not_4_out, j_k_ff_2_q[2]);
  not not_5 (not_5_out, j_k_ff_2_q[3]);
  not not_6 (not_6_out, nor_2_out);
  not not_7 (not_7_out, j_k_ff_3_q[0]);
  not not_8 (not_8_out, j_k_ff_3_q[1]);
  not not_9 (not_9_out, j_k_ff_3_q[2]);
  not not_10 (not_10_out, j_k_ff_3_q[3]);
  and and_10 (and_10_out, nor_3_out, not_11_out);
  not not_11 (not_11_out, nor_2_out);
  and and_11 (and_11_out, in_1, j_k_ff_1_q);
  and and_12 (and_12_out, in_1, j_k_ff_1_qn);
  or or_12 (or_12_out, and_42_out, and_9_out);
  or or_13 (or_13_out, and_45_out, and_10_out);
  J_K_Flip_Flop #(.trigger("falling")) j_k_ff_2 (
    .J(in_1), .K(in_1), .clk(buffer_2_out), .Q(j_k_ff_2_q[0]), .Qn(j_k_ff_2_qn), .preset(or_12_out),
    .reset(and_41_out));
  not not_12 (not_12_out, nor_2_out);
  J_K_Flip_Flop #(.trigger("falling")) j_k_ff_3 (
    .J(in_1), .K(in_1), .clk(or_13_out), .Q(j_k_ff_3_q[0]), .Qn(j_k_ff_3_qn), .reset(and_42_out));  // open: preset
  not not_13 (not_13_out, nor_2_out);
  and and_13 (and_13_out, or_2_out, nand_1_out);
  and and_14 (and_14_out, and_2_out, nand_2_out);
  and and_15 (and_15_out, and_3_out, nand_3_out);
  and and_16 (and_16_out, and_4_out, nand_4_out);
  and and_17 (and_17_out, and_5_out, nand_5_out);
  and and_18 (and_18_out, and_6_out, nand_6_out);
  and and_19 (and_19_out, and_7_out, nand_7_out);
  and and_20 (and_20_out, not_14_out, and_8_out);
  and and_21 (and_21_out, nor_2_out, j_k_ff_2_q[0]);
  and and_22 (and_22_out, j_k_ff_2_qn, not_12_out);
  and and_23 (and_23_out, nor_2_out, j_k_ff_3_q[0]);
  and and_24 (and_24_out, j_k_ff_3_qn, not_13_out);
  LED led_1 (.in(and_11_out));
  LED led_2 (.in(and_12_out));
  not not_14 (not_14_out, button_2_out);
  nand nand_1 (nand_1_out, not_15_out, button_2_out);
  not not_15 (not_15_out, d_ff_2_q);
  nand nand_2 (nand_2_out, not_16_out, button_2_out);
  not not_16 (not_16_out, d_ff_3_q);
  nand nand_3 (nand_3_out, not_17_out, button_2_out);
  not not_17 (not_17_out, d_ff_4_q);
  nand nand_4 (nand_4_out, not_18_out, button_2_out);
  not not_18 (not_18_out, d_ff_5_q);
  nand nand_5 (nand_5_out, not_19_out, button_2_out);
  not not_19 (not_19_out, d_ff_6_q);
  nand nand_6 (nand_6_out, not_20_out, button_2_out);
  not not_20 (not_20_out, d_ff_7_q);
  nand nand_7 (nand_7_out, not_21_out, button_2_out);
  not not_21 (not_21_out, d_ff_8_q);
  J_K_Flip_Flop #(.trigger("falling")) j_k_ff_4 (
    .J(or_14_out), .K(or_14_out), .clk(buffer_2_out), .Q(j_k_ff_2_q[1]), .Qn(j_k_ff_4_qn), .reset(or_15_out));  // open: preset
  or or_14 (or_14_out, and_21_out, and_22_out);
  or or_15 (or_15_out, and_43_out, and_41_out);
  J_K_Flip_Flop #(.trigger("falling")) j_k_ff_5 (
    .J(or_16_out), .K(or_16_out), .clk(or_13_out), .Q(j_k_ff_3_q[1]), .Qn(j_k_ff_5_qn), .reset(or_17_out));  // open: preset
  or or_16 (or_16_out, and_23_out, and_24_out);
  or or_17 (or_17_out, and_44_out, and_42_out);
  and and_25 (and_25_out, and_21_out, j_k_ff_2_q[1]);
  and and_26 (and_26_out, j_k_ff_4_qn, and_22_out);
  and and_27 (and_27_out, and_23_out, j_k_ff_3_q[1]);
  and and_28 (and_28_out, j_k_ff_5_qn, and_24_out);
  or or_18 (or_18_out, and_25_out, and_26_out);
  or or_19 (or_19_out, and_27_out, and_28_out);
  J_K_Flip_Flop #(.trigger("falling")) j_k_ff_6 (
    .J(or_18_out), .K(or_18_out), .clk(buffer_2_out), .Q(j_k_ff_2_q[2]), .Qn(j_k_ff_6_qn), .reset(or_20_out));  // open: preset
  or or_20 (or_20_out, and_43_out, and_41_out);
  J_K_Flip_Flop #(.trigger("falling")) j_k_ff_7 (
    .J(or_19_out), .K(or_19_out), .clk(or_13_out), .Q(j_k_ff_3_q[2]), .Qn(j_k_ff_7_qn), .reset(or_21_out));  // open: preset
  or or_21 (or_21_out, and_44_out, and_42_out);
  and and_29 (and_29_out, d_ff_1_q, in_1);
  and and_30 (and_30_out, d_ff_2_q, in_1);
  and and_31 (and_31_out, d_ff_3_q, in_1);
  and and_32 (and_32_out, d_ff_4_q, in_1);
  and and_33 (and_33_out, d_ff_5_q, in_1);
  and and_34 (and_34_out, d_ff_6_q, in_1);
  and and_35 (and_35_out, d_ff_7_q, in_1);
  and and_36 (and_36_out, d_ff_8_q, in_1);
  and and_37 (and_37_out, and_25_out, j_k_ff_2_q[2]);
  and and_38 (and_38_out, j_k_ff_6_qn, and_26_out);
  and and_39 (and_39_out, and_27_out, j_k_ff_3_q[2]);
  and and_40 (and_40_out, j_k_ff_7_qn, and_28_out);
  J_K_Flip_Flop #(.trigger("falling")) j_k_ff_8 (
    .J(or_22_out), .K(or_22_out), .clk(buffer_2_out), .Q(j_k_ff_2_q[3]), .preset(and_9_out),
    .reset(and_41_out));  // open: Qn
  or or_22 (or_22_out, and_37_out, and_38_out);
  J_K_Flip_Flop #(.trigger("falling")) j_k_ff_9 (
    .J(or_23_out), .K(or_23_out), .clk(or_13_out), .Q(j_k_ff_3_q[3]), .reset(and_42_out));  // open: Qn, preset
  or or_23 (or_23_out, and_39_out, and_40_out);
  LED led_3 (.in(and_36_out));
  LED led_4 (.in(and_35_out));
  LED led_5 (.in(and_34_out));
  LED led_6 (.in(and_33_out));
  LED led_7 (.in(and_32_out));
  LED led_8 (.in(and_31_out));
  LED led_9 (.in(and_30_out));
  LED led_10 (.in(and_29_out));
  or or_24 (or_24_out, j_k_ff_2_q[1], j_k_ff_2_q[2]);
  and and_41 (and_41_out, j_k_ff_2_q[3], nor_2_out, j_k_ff_2_q[1]);
  or or_25 (or_25_out, j_k_ff_3_q[1], j_k_ff_3_q[2]);
  and and_42 (and_42_out, j_k_ff_3_q[3], nor_2_out, j_k_ff_3_q[1]);
  and and_43 (and_43_out, j_k_ff_2_q[3], or_24_out, j_k_ff_2_q[0]);
  and and_44 (and_44_out, j_k_ff_3_q[3], or_25_out, j_k_ff_3_q[0]);
  nor nor_3 (nor_3_out, j_k_ff_2_q[0], j_k_ff_2_q[1], j_k_ff_2_q[2], j_k_ff_2_q[3]);
  and and_45 (and_45_out, j_k_ff_2_q[0], nor_2_out, j_k_ff_2_q[3]);
  assign and_46_out = {4{in_1}} & j_k_ff_2_q;  // AND_Gate and_46, 4 bits wide
  assign and_47_out = j_k_ff_3_q & {4{in_1}};  // AND_Gate and_47, 4 bits wide
  Hex_Digit_Display hex_digit_display_1 (.value(and_47_out));  // open: dp
  Hex_Digit_Display hex_digit_display_2 (.value(and_46_out));  // open: dp

  // Notes on the sheet:
  //   ON / OFF
  //   VOLUME ++
  //   VOLUME - -
  //   PLAY
  //   PAUSE
  //   NEXT >>
  //   PREVIOUS <<
  //   adding
  //   Play_State
  //   Pause_State
  //   VOLUME
  //   prev <<
  //   next >>
  //   TRACK
endmodule
