// Logisim project Assignment1.circ as structural Verilog: 1 circuit, main circuit main
module main (
  input  ON___OFF
);

  wire and_1_out, and_2_out, and_3_out, and_4_out, and_5_out, and_6_out, and_7_out, and_8_out, and_9_out,
       and_10_out, and_11_out, and_12_out, and_13_out, and_14_out, and_15_out, and_16_out, and_17_out,
       and_18_out, and_19_out, and_20_out, and_21_out, and_22_out, and_23_out, and_24_out, and_25_out,
       and_26_out, and_27_out, and_28_out, and_29_out, and_30_out, and_31_out, and_32_out, and_33_out,
       and_34_out, and_35_out, and_36_out, and_37_out, and_38_out, and_39_out, buffer_1_out, buffer_2_out,
       buffer_3_out, buffer_4_out, buffer_5_out, buffer_6_out, buffer_7_out, buffer_8_out, buffer_9_out,
       buffer_10_out, buffer_11_out, buffer_12_out, buffer_13_out, buffer_14_out, buffer_15_out,
       buffer_16_out, buffer_17_out, button_1_out, button_2_out, button_3_out, button_4_out, d_ff_1_q,
       d_ff_2_q, d_ff_3_q, j_k_ff_1_qn, j_k_ff_2_qn, j_k_ff_3_q, j_k_ff_3_qn, j_k_ff_4_qn, j_k_ff_5_qn,
       j_k_ff_6_qn, j_k_ff_7_qn, nand_1_out, nor_1_out, nor_2_out, nor_3_out, not_1_out, not_2_out,
       not_3_out, not_4_out, not_5_out, not_6_out, not_7_out, not_8_out, not_9_out, not_10_out, not_11_out,
       not_12_out, not_13_out, not_14_out, not_15_out, not_16_out, not_17_out, not_18_out, or_1_out,
       or_2_out, or_3_out, or_4_out, or_5_out, or_6_out, or_7_out, or_8_out, or_9_out, or_10_out, or_11_out,
       or_12_out, or_13_out, or_14_out, or_15_out, or_16_out, or_17_out, or_18_out, or_19_out, or_20_out,
       or_21_out, or_22_out, or_23_out, PAUSE_out, PLAY_out, xor_1_out, xor_2_out, xor_3_out, xor_4_out,
       xor_5_out;
  wire [3:0] and_40_out, and_41_out, j_k_ff_1_q, j_k_ff_2_q;

  Button button_1 (.out(button_1_out));
  Button button_2 (.out(button_2_out));
  nor nor_1 (nor_1_out, button_1_out, nor_2_out);
  nor nor_2 (nor_2_out, nor_1_out, button_2_out);
  buf buffer_1 (buffer_1_out, nor_2_out);
  or or_1 (or_1_out, button_1_out, button_2_out);
  buf buffer_2 (buffer_2_out, buffer_3_out);
  buf buffer_3 (buffer_3_out, buffer_4_out);
  buf buffer_4 (buffer_4_out, buffer_1_out);
  buf buffer_5 (buffer_5_out, buffer_2_out);
  not not_1 (not_1_out, buffer_6_out);
  Button PLAY (.out(PLAY_out));
  Button PAUSE (.out(PAUSE_out));
  Button button_3 (.out(button_3_out));
  Button button_4 (.out(button_4_out));
  or or_2 (or_2_out, and_29_out, and_1_out);
  buf buffer_6 (buffer_6_out, buffer_7_out);
  buf buffer_7 (buffer_7_out, buffer_9_out);
  buf buffer_8 (buffer_8_out, buffer_5_out);
  buf buffer_9 (buffer_9_out, buffer_8_out);
  not not_2 (not_2_out, j_k_ff_1_q[0]);
  not not_3 (not_3_out, j_k_ff_1_q[1]);
  not not_4 (not_4_out, j_k_ff_1_q[2]);
  not not_5 (not_5_out, j_k_ff_1_q[3]);
  and and_1 (and_1_out, not_2_out, not_3_out, not_4_out, not_5_out, not_6_out, not_7_out, not_8_out, not_9_out, not_10_out);
  not not_6 (not_6_out, buffer_6_out);
  not not_7 (not_7_out, j_k_ff_2_q[0]);
  not not_8 (not_8_out, j_k_ff_2_q[1]);
  not not_9 (not_9_out, j_k_ff_2_q[2]);
  not not_10 (not_10_out, j_k_ff_2_q[3]);
  and and_2 (and_2_out, nor_3_out, not_1_out);
  J_K_Flip_Flop j_k_ff_1 (
    .J(ON___OFF), .K(ON___OFF), .clk(or_1_out), .Q(j_k_ff_1_q[0]), .Qn(j_k_ff_1_qn), .preset(or_2_out),
    .reset(and_28_out));
  J_K_Flip_Flop j_k_ff_2 (
    .J(ON___OFF), .K(ON___OFF), .clk(or_3_out), .Q(j_k_ff_2_q[0]), .Qn(j_k_ff_2_qn), .reset(and_29_out));  // open: preset
  or or_3 (or_3_out, and_39_out, and_2_out);
  or or_4 (or_4_out, d_ff_3_q, d_ff_2_q, d_ff_1_q);
  nand nand_1 (nand_1_out, d_ff_3_q, d_ff_2_q, d_ff_1_q);
  not not_11 (not_11_out, buffer_6_out);
  or or_5 (or_5_out, PLAY_out, PAUSE_out);
  and and_3 (and_3_out, button_3_out, or_4_out);
  and and_4 (and_4_out, button_4_out, nand_1_out);
  and and_5 (and_5_out, buffer_6_out, j_k_ff_1_q[0]);
  and and_6 (and_6_out, j_k_ff_1_qn, not_11_out);
  and and_7 (and_7_out, buffer_6_out, j_k_ff_2_q[0]);
  and and_8 (and_8_out, j_k_ff_2_qn, not_12_out);
  not not_12 (not_12_out, buffer_6_out);
  or or_6 (or_6_out, and_5_out, and_6_out);
  or or_7 (or_7_out, and_7_out, and_8_out);
  J_K_Flip_Flop j_k_ff_3 (
    .J(or_5_out), .K(PAUSE_out), .clk(or_5_out), .Q(j_k_ff_3_q), .Qn(j_k_ff_3_qn), .reset(not_13_out));  // open: preset
  or or_8 (or_8_out, and_3_out, and_4_out);
  J_K_Flip_Flop j_k_ff_4 (
    .J(or_6_out), .K(or_6_out), .clk(or_1_out), .Q(j_k_ff_1_q[1]), .Qn(j_k_ff_4_qn), .reset(or_9_out));  // open: preset
  or or_9 (or_9_out, and_30_out, and_28_out);
  J_K_Flip_Flop j_k_ff_5 (
    .J(or_7_out), .K(or_7_out), .clk(or_3_out), .Q(j_k_ff_2_q[1]), .Qn(j_k_ff_5_qn), .reset(or_10_out));  // open: preset
  or or_10 (or_10_out, and_31_out, and_29_out);
  not not_13 (not_13_out, ON___OFF);
  xor xor_1 (xor_1_out, and_3_out, and_14_out);
  and and_9 (and_9_out, and_14_out, and_3_out);
  buf buffer_10 (buffer_10_out, or_8_out);
  and and_10 (and_10_out, and_5_out, j_k_ff_1_q[1]);
  and and_11 (and_11_out, j_k_ff_4_qn, and_6_out);
  and and_12 (and_12_out, and_7_out, j_k_ff_2_q[1]);
  and and_13 (and_13_out, j_k_ff_5_qn, and_8_out);
  xor xor_2 (xor_2_out, or_15_out, and_3_out);
  and and_14 (and_14_out, d_ff_3_q, or_8_out);
  buf buffer_11 (buffer_11_out, buffer_10_out);
  buf buffer_12 (buffer_12_out, buffer_14_out);
  buf buffer_13 (buffer_13_out, buffer_11_out);
  buf buffer_14 (buffer_14_out, buffer_13_out);
  xor xor_3 (xor_3_out, d_ff_1_q, xor_2_out);
  xor xor_4 (xor_4_out, d_ff_2_q, xor_1_out);
  and and_15 (and_15_out, d_ff_2_q, xor_1_out);
  xor xor_5 (xor_5_out, or_8_out, d_ff_3_q);
  buf buffer_15 (buffer_15_out, buffer_12_out);
  buf buffer_16 (buffer_16_out, buffer_15_out);
  buf buffer_17 (buffer_17_out, buffer_16_out);
  J_K_Flip_Flop j_k_ff_6 (
    .J(or_11_out), .K(or_11_out), .clk(or_1_out), .Q(j_k_ff_1_q[2]), .Qn(j_k_ff_6_qn), .reset(or_12_out));  // open: preset
  or or_11 (or_11_out, and_10_out, and_11_out);
  or or_12 (or_12_out, and_30_out, and_28_out);
  J_K_Flip_Flop j_k_ff_7 (
    .J(or_13_out), .K(or_13_out), .clk(or_3_out), .Q(j_k_ff_2_q[2]), .Qn(j_k_ff_7_qn), .reset(or_14_out));  // open: preset
  or or_13 (or_13_out, and_12_out, and_13_out);
  or or_14 (or_14_out, and_31_out, and_29_out);
  and and_16 (and_16_out, ON___OFF, j_k_ff_3_q);
  and and_17 (and_17_out, ON___OFF, j_k_ff_3_qn);
  or or_15 (or_15_out, and_15_out, and_9_out);
  D_Flip_Flop d_ff_1 (.D(xor_3_out), .clk(buffer_17_out), .Q(d_ff_1_q));  // open: Qn, preset, reset
  D_Flip_Flop d_ff_2 (.D(xor_4_out), .clk(buffer_17_out), .Q(d_ff_2_q));  // open: Qn, preset, reset
  D_Flip_Flop d_ff_3 (.D(xor_5_out), .clk(buffer_17_out), .Q(d_ff_3_q));  // open: Qn, preset, reset
  and and_18 (and_18_out, and_10_out, j_k_ff_1_q[2]);
  and and_19 (and_19_out, j_k_ff_6_qn, and_11_out);
  and and_20 (and_20_out, and_12_out, j_k_ff_2_q[2]);
  and and_21 (and_21_out, j_k_ff_7_qn, and_13_out);
  J_K_Flip_Flop j_k_ff_8 (
    .J(or_16_out), .K(or_16_out), .clk(or_1_out), .Q(j_k_ff_1_q[3]), .preset(and_1_out), .reset(and_28_out));  // open: Qn
  or or_16 (or_16_out, and_18_out, and_19_out);
  J_K_Flip_Flop j_k_ff_9 (
    .J(or_17_out), .K(or_17_out), .clk(or_3_out), .Q(j_k_ff_2_q[3]), .reset(and_29_out));  // open: Qn, preset
  or or_17 (or_17_out, and_20_out, and_21_out);
  not not_14 (not_14_out, d_ff_2_q);
  not not_15 (not_15_out, d_ff_1_q);
  not not_16 (not_16_out, d_ff_3_q);
  not not_17 (not_17_out, d_ff_1_q);
  not not_18 (not_18_out, d_ff_2_q);
  and and_22 (and_22_out, d_ff_3_q, not_14_out, not_15_out);
  and and_23 (and_23_out, not_16_out, d_ff_2_q, not_17_out);
  and and_24 (and_24_out, d_ff_3_q, d_ff_2_q);
  and and_25 (and_25_out, d_ff_3_q, not_18_out, d_ff_1_q);
  and and_26 (and_26_out, d_ff_2_q, d_ff_1_q);
  and and_27 (and_27_out, d_ff_3_q, d_ff_2_q, d_ff_1_q);
  and and_28 (and_28_out, j_k_ff_1_q[3], j_k_ff_1_q[1]);
  or or_18 (or_18_out, j_k_ff_2_q[1], j_k_ff_2_q[2]);
  and and_29 (and_29_out, j_k_ff_2_q[3], buffer_6_out, j_k_ff_2_q[1]);
  or or_19 (or_19_out, and_22_out, or_20_out);
  or or_20 (or_20_out, and_23_out, or_21_out);
  or or_21 (or_21_out, and_24_out, d_ff_1_q);
  or or_22 (or_22_out, j_k_ff_1_q[1], j_k_ff_1_q[2]);
  and and_30 (and_30_out, j_k_ff_1_q[3], or_22_out, j_k_ff_1_q[0]);
  and and_31 (and_31_out, j_k_ff_2_q[3], or_18_out, j_k_ff_2_q[0]);
  or or_23 (or_23_out, and_25_out, and_26_out);
  nor nor_3 (nor_3_out, j_k_ff_1_q[0], j_k_ff_1_q[1], j_k_ff_1_q[2], j_k_ff_1_q[3]);
  and and_32 (and_32_out, ON___OFF, or_19_out);
  and and_33 (and_33_out, ON___OFF, or_20_out);
  and and_34 (and_34_out, ON___OFF, or_21_out);
  and and_35 (and_35_out, ON___OFF, d_ff_1_q);
  and and_36 (and_36_out, ON___OFF, or_23_out);
  and and_37 (and_37_out, ON___OFF, and_26_out);
  and and_38 (and_38_out, ON___OFF, and_27_out);
  and and_39 (and_39_out, j_k_ff_1_q[0], buffer_6_out, j_k_ff_1_q[3]);
  LED Played_State (.in(and_16_out));
  LED Paused_State (.in(and_17_out));
  Hex_Digit_Display hex_digit_display_1 (.value(and_40_out));  // open: dp
  assign and_40_out = j_k_ff_2_q & {4{ON___OFF}};  // AND_Gate and_40, 4 bits wide
  Hex_Digit_Display hex_digit_display_2 (.value(and_41_out));  // open: dp
  assign and_41_out = {4{ON___OFF}} & j_k_ff_1_q;  // AND_Gate and_41, 4 bits wide
  LED led_1 (.in(ON___OFF));
  LED led_2 (.in(and_38_out));
  LED led_3 (.in(and_37_out));
  LED led_4 (.in(and_36_out));
  LED led_5 (.in(and_35_out));
  LED led_6 (.in(and_34_out));
  LED led_7 (.in(and_33_out));
  LED led_8 (.in(and_32_out));

  // Notes on the sheet:
  //   Volume ++
  //   Volume - -
  //   VOLUME
endmodule
