// Logisim project Circuit1.circ as structural Verilog: 1 circuit, main circuit main
module main (
  input  pin1,
  input  pin2
);

  wire and_1_out;

  and and_1 (and_1_out, pin1, pin2);
  LED led_1 (.in(and_1_out));
endmodule
