// Logisim project Circuit2.circ as structural Verilog: 1 circuit, main circuit main
module main (
  input  piny
);

  wire not_1_out;

  not not_1 (not_1_out, piny);
  LED led_1 (.in(not_1_out));
endmodule
