// Logisim project Circuit3.circ as structural Verilog: 1 circuit, main circuit main
module main (
  input  in_1,
  input  in_2
);

  wire nand_1_out;

  nand nand_1 (nand_1_out, in_1, in_2);
  LED led_1 (.in(nand_1_out));
endmodule
