// Logisim project Circuit4.circ as structural Verilog: 1 circuit, main circuit main
module main (
  input  X,
  input  Y
);

  wire and_1_out, xor_1_out;

  xor xor_1 (xor_1_out, X, Y);
  and and_1 (and_1_out, X, Y);
  LED Sum_output (.in(xor_1_out));
  LED Carry_output (.in(and_1_out));
endmodule
