// Logisim project Circuit5.circ as structural Verilog: 1 circuit, main circuit main
module main (
  input  Carry_in_bit,
  input  X,
  input  Y
);

  wire and_1_out, and_2_out, or_1_out, xor_1_out, xor_2_out;

  and and_1 (and_1_out, X, Y);
  xor xor_1 (xor_1_out, X, Y);
  xor xor_2 (xor_2_out, Carry_in_bit, xor_1_out);
  and and_2 (and_2_out, Carry_in_bit, xor_1_out);
  or or_1 (or_1_out, and_2_out, and_1_out);
  LED Output_bit_0 (.in(xor_2_out));
  LED Carry_out_bit (.in(or_1_out));
endmodule
