// Logisim project part1.circ as structural Verilog: 1 circuit, main circuit main
module main (
  input  x1,
  input  y1,
  input  x2,
  input  y2,
  input  x3,
  input  y3,
  input  x4,
  input  y4
);

  wire and_1_out, and_2_out, and_3_out, and_4_out, and_5_out, and_6_out, and_7_out, or_1_out, or_2_out,
       or_3_out, xor_1_out, xor_2_out, xor_3_out, xor_4_out, xor_5_out, xor_6_out, xor_7_out;

  xor xor_1 (xor_1_out, x1, y1);
  and and_1 (and_1_out, x1, y1);
  xor xor_2 (xor_2_out, x2, y2);
  and and_2 (and_2_out, x2, y2);
  xor xor_3 (xor_3_out, x3, y3);
  and and_3 (and_3_out, x3, y3);
  xor xor_4 (xor_4_out, x4, y4);
  and and_4 (and_4_out, x4, y4);
  xor xor_5 (xor_5_out, and_1_out, xor_2_out);
  and and_5 (and_5_out, and_1_out, xor_2_out);
  xor xor_6 (xor_6_out, or_1_out, xor_3_out);
  and and_6 (and_6_out, or_1_out, xor_3_out);
  xor xor_7 (xor_7_out, or_2_out, xor_4_out);
  and and_7 (and_7_out, or_2_out, xor_4_out);
  or or_1 (or_1_out, and_5_out, and_2_out);
  or or_2 (or_2_out, and_6_out, and_3_out);
  or or_3 (or_3_out, and_7_out, and_4_out);
  LED Carry_in_bit_1 (.in(and_1_out));
  LED Carry_in_bit_2 (.in(or_1_out));
  LED Carry_in_bit_3 (.in(or_2_out));
  LED Carry_in_bit_4 (.in(or_3_out));
  LED Output1 (.in(xor_1_out));
  LED Output2 (.in(xor_5_out));
  LED Output3 (.in(xor_6_out));
  LED Output4 (.in(xor_7_out));
endmodule
