// Logisim project part3.circ as structural Verilog: 1 circuit, main circuit main
module main (
  input  Data
);

  wire nand_1_out, nand_2_out, nor_1_out, nor_2_out, not_1_out;

  Clock clock_1 (.out(Data));
  not not_1 (not_1_out, Data);
  nand nand_1 (nand_1_out, not_1_out, Data);
  nand nand_2 (nand_2_out, Data, Data);
  nor nor_1 (nor_1_out, nand_1_out, nor_2_out);
  nor nor_2 (nor_2_out, nor_1_out, nand_2_out);
  LED led_1 (.in(nor_1_out));
  LED led_2 (.in(nor_2_out));

  // Notes on the sheet:
  //   Clock
  //   Q
  //   Q'
endmodule
