// Logisim project 3.1.circ as structural Verilog: 1 circuit, main circuit main
module main (
  input  in_1,
  input  in_2,
  input  in_3,
  input  in_4,
  input  in_5,
  input  in_6,
  input  in_7,
  input  in_8,
  input  in_9
);

  wire and_1_out, and_2_out, clock_1_out, clock_2_out, clock_3_out, d_ff_1_q, d_ff_2_q, d_ff_3_q, d_ff_4_q,
       j_k_ff_1_q, j_k_ff_3_q, j_k_ff_5_q;
  wire [2:0] j_k_ff_2_q;

  Clock clock_1 (.out(clock_1_out));
  Clock clock_2 (.out(clock_2_out));
  Clock clock_3 (.out(clock_3_out));
  D_Flip_Flop d_ff_1 (.clk(clock_1_out), .D(in_1), .Q(d_ff_1_q), .reset(in_5));  // open: Qn, preset
  LED led_1 (.in(d_ff_1_q));
  J_K_Flip_Flop j_k_ff_1 (.J(in_6), .clk(j_k_ff_3_q), .K(in_6), .Q(j_k_ff_1_q), .reset(in_7));  // open: Qn, preset
  LED led_2 (.in(j_k_ff_1_q));
  J_K_Flip_Flop j_k_ff_2 (
    .J(in_8), .clk(clock_3_out), .K(in_8), .Q(j_k_ff_2_q[0]), .reset(and_2_out));  // open: Qn, preset
  D_Flip_Flop d_ff_2 (.clk(clock_1_out), .D(in_2), .Q(d_ff_2_q), .reset(in_5));  // open: Qn, preset
  LED led_3 (.in(j_k_ff_2_q[0]));
  LED led_4 (.in(d_ff_2_q));
  J_K_Flip_Flop j_k_ff_3 (.J(in_6), .clk(j_k_ff_5_q), .K(in_6), .Q(j_k_ff_3_q), .reset(in_7));  // open: Qn, preset
  LED led_5 (.in(j_k_ff_3_q));
  and and_1 (and_1_out, j_k_ff_2_q[0], j_k_ff_2_q[1]);
  J_K_Flip_Flop j_k_ff_4 (
    .J(j_k_ff_2_q[0]), .clk(clock_3_out), .K(j_k_ff_2_q[0]), .Q(j_k_ff_2_q[1]), .reset(and_2_out));  // open: Qn, preset
  LED led_6 (.in(j_k_ff_2_q[1]));
  D_Flip_Flop d_ff_3 (.clk(clock_1_out), .D(in_3), .Q(d_ff_3_q), .reset(in_5));  // open: Qn, preset
  LED led_7 (.in(d_ff_3_q));
  J_K_Flip_Flop j_k_ff_5 (.J(in_6), .clk(clock_2_out), .K(in_6), .Q(j_k_ff_5_q), .reset(in_7));  // open: Qn, preset
  J_K_Flip_Flop j_k_ff_6 (
    .J(and_1_out), .clk(clock_3_out), .K(and_1_out), .Q(j_k_ff_2_q[2]), .reset(and_2_out));  // open: Qn, preset
  D_Flip_Flop d_ff_4 (.clk(clock_1_out), .D(in_4), .Q(d_ff_4_q), .reset(in_5));  // open: Qn, preset
  LED led_8 (.in(d_ff_4_q));
  LED led_9 (.in(j_k_ff_5_q));
  LED led_10 (.in(j_k_ff_2_q[2]));
  and and_2 (and_2_out, j_k_ff_2_q[2], j_k_ff_2_q[1]);
  Hex_Digit_Display hex_digit_display_1 (.value({in_9, j_k_ff_2_q}));  // open: dp
endmodule
