// Logisim project Lab4.circ as structural Verilog: 1 circuit, main circuit main
module main (
  input  in_1,
  input  in_2,
  input  in_3,
  input  in_4,
  input  in_5,
  input  in_6,
  input  in_7,
  input  in_8,
  input  in_9
);

  wire and_1_out, and_2_out, and_3_out, and_4_out, and_5_out, and_6_out, and_7_out, and_8_out, and_9_out,
       and_10_out, and_11_out, and_12_out, and_13_out, and_14_out, and_15_out, and_16_out, clock_1_out,
       clock_2_out, clock_3_out, j_k_ff_1_q, j_k_ff_2_q, j_k_ff_2_qn, j_k_ff_3_q, j_k_ff_4_q, j_k_ff_5_q,
       j_k_ff_5_qn, j_k_ff_6_q, j_k_ff_7_q, j_k_ff_8_q, j_k_ff_9_q, not_1_out, not_2_out, not_3_out,
       not_4_out, not_5_out, not_6_out, not_7_out, or_1_out, or_2_out, or_3_out, or_4_out, or_5_out,
       or_6_out, or_7_out, or_8_out, or_9_out;

  Clock clock_1 (.out(clock_1_out));
  Clock clock_2 (.out(clock_2_out));
  not not_1 (not_1_out, in_3);
  buf and_1 (and_1_out, in_3);  // AND_Gate
  and and_2 (and_2_out, not_1_out, in_5);
  not not_2 (not_2_out, in_6);
  and and_3 (and_3_out, in_9, in_6);
  or or_1 (or_1_out, in_1, in_2);
  or or_2 (or_2_out, and_2_out, and_1_out);
  or or_3 (or_3_out, and_3_out, and_4_out);
  LED led_1 (.in(or_1_out));
  not not_3 (not_3_out, in_3);
  J_K_Flip_Flop j_k_ff_1 (.J(or_2_out), .K(clock_1_out), .Q(j_k_ff_1_q));  // open: clk, Qn, preset, reset
  LED led_2 (.in(j_k_ff_1_q));
  and and_4 (and_4_out, not_2_out, j_k_ff_5_q);
  J_K_Flip_Flop j_k_ff_2 (.J(or_3_out), .K(clock_2_out), .Q(j_k_ff_2_q), .Qn(j_k_ff_2_qn));  // open: clk, preset, reset
  and and_5 (and_5_out, not_3_out, j_k_ff_1_q);
  or or_4 (or_4_out, and_5_out, and_6_out);
  LED led_3 (.in(j_k_ff_2_qn));
  buf and_6 (and_6_out, in_3);  // AND_Gate
  not not_4 (not_4_out, in_3);
  J_K_Flip_Flop j_k_ff_3 (.J(or_4_out), .K(clock_1_out), .Q(j_k_ff_3_q));  // open: clk, Qn, preset, reset
  LED led_4 (.in(j_k_ff_3_q));
  and and_7 (and_7_out, j_k_ff_2_q, in_6);
  and and_8 (and_8_out, not_4_out, j_k_ff_3_q);
  and and_9 (and_9_out, not_2_out, in_7);
  or or_5 (or_5_out, and_7_out, and_9_out);
  buf and_10 (and_10_out, in_3);  // AND_Gate
  or or_6 (or_6_out, and_8_out, and_10_out);
  J_K_Flip_Flop j_k_ff_4 (.J(or_6_out), .K(clock_1_out), .Q(j_k_ff_4_q));  // open: clk, Qn, preset, reset
  J_K_Flip_Flop j_k_ff_5 (.J(or_5_out), .K(clock_2_out), .Q(j_k_ff_5_q), .Qn(j_k_ff_5_qn));  // open: clk, preset, reset
  LED led_5 (.in(j_k_ff_5_qn));
  not not_5 (not_5_out, in_3);
  and and_11 (and_11_out, not_5_out, j_k_ff_4_q);
  LED led_6 (.in(j_k_ff_4_q));
  buf and_12 (and_12_out, in_3);  // AND_Gate
  or or_7 (or_7_out, and_11_out, and_12_out);
  not not_6 (not_6_out, in_3);
  J_K_Flip_Flop j_k_ff_6 (.J(or_7_out), .K(clock_1_out), .Q(j_k_ff_6_q));  // open: clk, Qn, preset, reset
  LED led_7 (.in(j_k_ff_6_q));
  and and_13 (and_13_out, not_6_out, j_k_ff_6_q);
  and and_14 (and_14_out, in_3, in_4);
  or or_8 (or_8_out, and_13_out, and_14_out);
  Clock clock_3 (.out(clock_3_out));
  J_K_Flip_Flop j_k_ff_7 (.J(or_8_out), .K(clock_1_out), .Q(j_k_ff_7_q));  // open: clk, Qn, preset, reset
  not not_7 (not_7_out, in_8);
  LED led_8 (.in(j_k_ff_7_q));
  J_K_Flip_Flop j_k_ff_8 (.J(not_7_out), .K(clock_3_out), .Q(j_k_ff_8_q));  // open: clk, Qn, preset, reset
  LED led_9 (.in(j_k_ff_8_q));
  and and_15 (and_15_out, j_k_ff_8_q, in_8);
  and and_16 (and_16_out, not_7_out, not_7_out);
  or or_9 (or_9_out, and_15_out, and_16_out);
  J_K_Flip_Flop j_k_ff_9 (.J(or_9_out), .K(clock_3_out), .Q(j_k_ff_9_q));  // open: clk, Qn, preset, reset
  LED led_10 (.in(j_k_ff_9_q));
endmodule
